# Fritzing sketch Arduino XBee Adapter Hack (saved by Fritzing 0.3.19b)
breadboards: 1

parts:
  Arduino1 = Arduino
  U1 = XBee

nets:
  GND: Arduino1.GND, U1.GND
  N1: Arduino1.D1TX, U1.pin2
  N2: Arduino1.D0RX, U1.pin3
  3V3: Arduino1.3V3, U1.VCC
