# Fritzing sketch Romantic Lighting Sensor BASE (saved by Fritzing 0.3.16b)
breadboards: 1

parts:
  Arduino1 = Arduino
  U1 = XBee
  LED1 = green LED - 5mm

nets:
  GND: Arduino1.GND, U1.GND, LED1.cathode
  N1: Arduino1.D11, LED1.anode
  N2: Arduino1.D1TX, U1.pin3
  N3: Arduino1.D0RX, U1.pin2
  3V3: Arduino1.3V3, U1.VCC
