# Fritzing sketch Romantic Lighting Sensor BASIC SENSOR (saved by Fritzing 0.3.19b)
breadboards: 1

parts:
  U1 = XBee
  R2_Variable_0_-_10K = Photocell (LDR) [package=THT]
  VCC1 = obsolete Battery
  R1_20kΩ = Resistor [resistance=20k package=THT]

nets:
  N1: U1.VCC, VCC1.+, R1_20kΩ.Pin_1
  N2: U1.GND, R2_Variable_0_-_10K.pin_0, VCC1.-
  N3: U1.pin20, R2_Variable_0_-_10K.pin_1, R1_20kΩ.Pin_0
