# Fritzing sketch Romantic Lighting Sensor FEEDBACK SENSOR (saved by Fritzing 0.3.19b)
breadboards: 1

parts:
  U1 = XBee
  R1_20kΩ = Resistor [resistance=20k package=THT]
  R2_Variable_0_-_10K = Photocell (LDR) [package=THT]
  VCC1 = obsolete Battery
  LED1 = green LED - 5mm

nets:
  N1: U1.VCC, R1_20kΩ.Pin_1, VCC1.+
  N2: U1.GND, R2_Variable_0_-_10K.pin_0, VCC1.-, LED1.cathode
  N3: U1.pin19, LED1.anode
  N4: U1.pin20, R1_20kΩ.Pin_0, R2_Variable_0_-_10K.pin_1
