# Fritzing sketch Simple Actuator Node (saved by Fritzing 0.3.19b)
breadboards: 1

parts:
  U1 = XBee
  Power_plug_5V~12V = Power plug
  2N3904 = NPN-Transistor [package="TO92 [THT]"]
  R2_10KΩ = Resistor [resistance=10k package=THT]
  C1_10µF = Electrolytic Capacitor [package=THT]
  C2_1µF = Electrolytic Capacitor [package=THT]
  relay_PowerSwitchTail = Relay [package=THT]
  U2_3_3V = Voltage Regulator - 3.3V [package="TO220 [THT]"]

nets:
  N1: U1.VCC, C2_1µF.+, U2_3_3V.output_voltage
  GND: U1.GND, Power_plug_5V~12V.GND, 2N3904.E, C1_10µF.-, C2_1µF.-, U2_3_3V.GND
  N2: U1.pin20, R2_10KΩ.Pin_0
  N3: Power_plug_5V~12V.VCC, C1_10µF.+, relay_PowerSwitchTail.COIL1, U2_3_3V.input_voltage
  N4: 2N3904.B, R2_10KΩ.Pin_1
  N5: 2N3904.C, relay_PowerSwitchTail.COIL2
