# Fritzing sketch Simple Sensor Node LM335 REGULATED (saved by Fritzing 0.3.19b)
breadboards: 1

parts:
  U1 = XBee
  Power_plug_5V~12V = Power plug
  R3_300KΩ = Resistor [resistance=300 package=THT]
  C1_10µF = Electrolytic Capacitor [package=THT]
  C2_1µF = Electrolytic Capacitor [package=THT]
  U2_3_3V = Voltage Regulator - 3.3V [package="TO220 [THT]"]
  U2_LM335 = mystery part, 3 pins [chip_label=LM335 spacing=300mil]
  R1_100KΩ = Resistor [resistance=100k package=THT]
  R2_200KΩ = Resistor [resistance=200k package=THT]

nets:
  N1: U1.VCC, R3_300KΩ.Pin_0, C2_1µF.+, U2_3_3V.output_voltage
  GND: U1.GND, Power_plug_5V~12V.GND, C1_10µF.-, C2_1µF.-, U2_3_3V.GND, U2_LM335.pin3, R1_100KΩ.Pin_0
  N2: U1.pin20, R1_100KΩ.Pin_1, R2_200KΩ.Pin_0
  N3: Power_plug_5V~12V.VCC, C1_10µF.+, U2_3_3V.input_voltage
  N4: R3_300KΩ.Pin_1, U2_LM335.pin2, R2_200KΩ.Pin_1
