# Fritzing sketch Twitter_Reader (saved by Fritzing 0.3.19b)
breadboards: 1

parts:
  Arduino1 = Arduino
  LCD1 = LCD screen
  U1 = XBee
  R1 = Rotary Potentiometer (Small)

nets:
  GND: Arduino1.GND, LCD1.VSS, LCD1.R/W, LCD1.LED-, R1.leg2
  N1: Arduino1.D12, LCD1.RS
  N2: Arduino1.D11, LCD1.E
  N3: Arduino1.D7, U1.pin3
  N4: Arduino1.D6, U1.pin2
  N5: Arduino1.D5, LCD1.DB4
  N6: Arduino1.D4, LCD1.DB5
  N7: Arduino1.D3, LCD1.DB6
  N8: Arduino1.D2, LCD1.DB7
  3V3: Arduino1.3V3, U1.VCC
  N9: LCD1.VDD, LCD1.LED+, R1.leg1
  N10: LCD1.V0, R1.wiper
