# Fritzing sketch XBee Arduino Basic Doorbell BELL (saved by Fritzing 0.3.15b)
breadboards: 1

parts:
  Arduino1 = Arduino
  U1 = XBee
  J1 = Piezo Speaker

nets:
  GND: Arduino1.GND, U1.GND, J1.pin2
  N1: Arduino1.D5, J1.pin1
  N2: Arduino1.D1TX, U1.pin3
  N3: Arduino1.D0RX, U1.pin2
  3V3: Arduino1.3V3, U1.VCC
