# Fritzing sketch XBee Arduino Feedback Doorbell-BUTTON (saved by Fritzing 0.3.15b)
breadboards: 1

parts:
  Arduino1 = Arduino
  U1 = XBee
  S1 = Pushbutton [package=THT]
  R1 = Resistor [resistance=220 package=THT]
  LED1 = green LED - 5mm

nets:
  GND: Arduino1.GND, U1.GND, R1.Pin_0, LED1.cathode
  N1: Arduino1.D11, LED1.anode
  N2: Arduino1.D2, S1.leg1, R1.Pin_1
  N3: Arduino1.D1TX, U1.pin3
  N4: Arduino1.D0RX, U1.pin2
  3V3: Arduino1.3V3, U1.VCC, S1.leg0
